// Digital circuit 16bite_sumator.dig as structural Verilog
module _16bite_sumator (
  input  A1,
  input  B1,
  input  Cary,
  input  B2,
  input  B3,
  input  B4,
  input  B5,
  input  B6,
  input  B7,
  input  B8,
  input  B9,
  input  B10,
  input  B11,
  input  B12,
  input  B13,
  input  B14,
  input  B15,
  input  B16,
  input  A2,
  input  A3,
  input  A4,
  input  A5,
  input  A6,
  input  A7,
  input  A8,
  input  A9,
  input  A10,
  input  A11,
  input  A12,
  input  A13,
  input  A14,
  input  A15,
  input  A16,
  output Out1,
  output Out2,
  output Out3,
  output Out4,
  output Out5,
  output Out6,
  output Out7,
  output Out8,
  output Out9,
  output Out10,
  output Out11,
  output Out12,
  output Out13,
  output Out14,
  output Out15,
  output Out16,
  output Out_cary
);

  wire sumator_1_cout, sumator_2_cout, sumator_6_cout, sumator_12_cout, sumator_17_cout, sumator_21_cout,
       sumator_26_cout, sumator_30_cout, sumator_35_cout, sumator_39_cout, sumator_44_cout, sumator_48_cout,
       sumator_53_cout, sumator_57_cout, sumator_62_cout;

  Sumator sumator_1 (.Cin(Cary), .A(A1), .B(B1), .Output(Out1), .Cout(sumator_1_cout));
  Sumator sumator_2 (.Cin(sumator_1_cout), .A(A2), .B(B2), .Output(Out2), .Cout(sumator_2_cout));
  Sumator sumator_3 (.Cin(sumator_1_cout), .A(A2), .B(B2), .Output(Out2), .Cout(sumator_2_cout));
  Sumator sumator_4 (.Cin(sumator_1_cout), .A(A2), .B(B2), .Output(Out2), .Cout(sumator_2_cout));
  Sumator sumator_5 (.Cin(sumator_1_cout), .A(A2), .B(B2), .Output(Out2), .Cout(sumator_2_cout));
  Sumator sumator_6 (.Cin(sumator_2_cout), .A(A3), .B(B3), .Output(Out3), .Cout(sumator_6_cout));
  Sumator sumator_7 (.Cin(sumator_2_cout), .A(A3), .B(B3), .Output(Out3), .Cout(sumator_6_cout));
  Sumator sumator_8 (.Cin(sumator_2_cout), .A(A3), .B(B3), .Output(Out3), .Cout(sumator_6_cout));
  Sumator sumator_9 (.Cin(sumator_2_cout), .A(A3), .B(B3), .Output(Out3), .Cout(sumator_6_cout));
  Sumator sumator_10 (.Cin(sumator_2_cout), .A(A3), .B(B3), .Output(Out3), .Cout(sumator_6_cout));
  Sumator sumator_11 (.Cin(sumator_2_cout), .A(A3), .B(B3), .Output(Out3), .Cout(sumator_6_cout));
  Sumator sumator_12 (.Cin(sumator_6_cout), .A(A4), .B(B4), .Output(Out4), .Cout(sumator_12_cout));
  Sumator sumator_13 (.Cin(sumator_6_cout), .A(A4), .B(B4), .Output(Out4), .Cout(sumator_12_cout));
  Sumator sumator_14 (.Cin(sumator_6_cout), .A(A4), .B(B4), .Output(Out4), .Cout(sumator_12_cout));
  Sumator sumator_15 (.Cin(sumator_6_cout), .A(A4), .B(B4), .Output(Out4), .Cout(sumator_12_cout));
  Sumator sumator_16 (.Cin(sumator_6_cout), .A(A4), .B(B4), .Output(Out4), .Cout(sumator_12_cout));
  Sumator sumator_17 (.Cin(sumator_12_cout), .A(A5), .B(B5), .Output(Out5), .Cout(sumator_17_cout));
  Sumator sumator_18 (.Cin(sumator_12_cout), .A(A5), .B(B5), .Output(Out5), .Cout(sumator_17_cout));
  Sumator sumator_19 (.Cin(sumator_12_cout), .A(A5), .B(B5), .Output(Out5), .Cout(sumator_17_cout));
  Sumator sumator_20 (.Cin(sumator_12_cout), .A(A5), .B(B5), .Output(Out5), .Cout(sumator_17_cout));
  Sumator sumator_21 (.Cin(sumator_17_cout), .A(A6), .B(B6), .Output(Out6), .Cout(sumator_21_cout));
  Sumator sumator_22 (.Cin(sumator_17_cout), .A(A6), .B(B6), .Output(Out6), .Cout(sumator_21_cout));
  Sumator sumator_23 (.Cin(sumator_17_cout), .A(A6), .B(B6), .Output(Out6), .Cout(sumator_21_cout));
  Sumator sumator_24 (.Cin(sumator_17_cout), .A(A6), .B(B6), .Output(Out6), .Cout(sumator_21_cout));
  Sumator sumator_25 (.Cin(sumator_17_cout), .A(A6), .B(B6), .Output(Out6), .Cout(sumator_21_cout));
  Sumator sumator_26 (.Cin(sumator_21_cout), .A(A7), .B(B7), .Output(Out7), .Cout(sumator_26_cout));
  Sumator sumator_27 (.Cin(sumator_21_cout), .A(A7), .B(B7), .Output(Out7), .Cout(sumator_26_cout));
  Sumator sumator_28 (.Cin(sumator_21_cout), .A(A7), .B(B7), .Output(Out7), .Cout(sumator_26_cout));
  Sumator sumator_29 (.Cin(sumator_21_cout), .A(A7), .B(B7), .Output(Out7), .Cout(sumator_26_cout));
  Sumator sumator_30 (.Cin(sumator_26_cout), .A(A8), .B(B8), .Output(Out8), .Cout(sumator_30_cout));
  Sumator sumator_31 (.Cin(sumator_26_cout), .A(A8), .B(B8), .Output(Out8), .Cout(sumator_30_cout));
  Sumator sumator_32 (.Cin(sumator_26_cout), .A(A8), .B(B8), .Output(Out8), .Cout(sumator_30_cout));
  Sumator sumator_33 (.Cin(sumator_26_cout), .A(A8), .B(B8), .Output(Out8), .Cout(sumator_30_cout));
  Sumator sumator_34 (.Cin(sumator_26_cout), .A(A8), .B(B8), .Output(Out8), .Cout(sumator_30_cout));
  Sumator sumator_35 (.Cin(sumator_30_cout), .A(A9), .B(B9), .Output(Out9), .Cout(sumator_35_cout));
  Sumator sumator_36 (.Cin(sumator_30_cout), .A(A9), .B(B9), .Output(Out9), .Cout(sumator_35_cout));
  Sumator sumator_37 (.Cin(sumator_30_cout), .A(A9), .B(B9), .Output(Out9), .Cout(sumator_35_cout));
  Sumator sumator_38 (.Cin(sumator_30_cout), .A(A9), .B(B9), .Output(Out9), .Cout(sumator_35_cout));
  Sumator sumator_39 (.Cin(sumator_35_cout), .A(A10), .B(B10), .Output(Out10), .Cout(sumator_39_cout));
  Sumator sumator_40 (.Cin(sumator_35_cout), .A(A10), .B(B10), .Output(Out10), .Cout(sumator_39_cout));
  Sumator sumator_41 (.Cin(sumator_35_cout), .A(A10), .B(B10), .Output(Out10), .Cout(sumator_39_cout));
  Sumator sumator_42 (.Cin(sumator_35_cout), .A(A10), .B(B10), .Output(Out10), .Cout(sumator_39_cout));
  Sumator sumator_43 (.Cin(sumator_35_cout), .A(A10), .B(B10), .Output(Out10), .Cout(sumator_39_cout));
  Sumator sumator_44 (.Cin(sumator_39_cout), .A(A11), .B(B11), .Output(Out11), .Cout(sumator_44_cout));
  Sumator sumator_45 (.Cin(sumator_39_cout), .A(A11), .B(B11), .Output(Out11), .Cout(sumator_44_cout));
  Sumator sumator_46 (.Cin(sumator_39_cout), .A(A11), .B(B11), .Output(Out11), .Cout(sumator_44_cout));
  Sumator sumator_47 (.Cin(sumator_39_cout), .A(A11), .B(B11), .Output(Out11), .Cout(sumator_44_cout));
  Sumator sumator_48 (.Cin(sumator_44_cout), .A(A12), .B(B12), .Output(Out12), .Cout(sumator_48_cout));
  Sumator sumator_49 (.Cin(sumator_44_cout), .A(A12), .B(B12), .Output(Out12), .Cout(sumator_48_cout));
  Sumator sumator_50 (.Cin(sumator_44_cout), .A(A12), .B(B12), .Output(Out12), .Cout(sumator_48_cout));
  Sumator sumator_51 (.Cin(sumator_44_cout), .A(A12), .B(B12), .Output(Out12), .Cout(sumator_48_cout));
  Sumator sumator_52 (.Cin(sumator_44_cout), .A(A12), .B(B12), .Output(Out12), .Cout(sumator_48_cout));
  Sumator sumator_53 (.Cin(sumator_48_cout), .A(A13), .B(B13), .Output(Out13), .Cout(sumator_53_cout));
  Sumator sumator_54 (.Cin(sumator_48_cout), .A(A13), .B(B13), .Output(Out13), .Cout(sumator_53_cout));
  Sumator sumator_55 (.Cin(sumator_48_cout), .A(A13), .B(B13), .Output(Out13), .Cout(sumator_53_cout));
  Sumator sumator_56 (.Cin(sumator_48_cout), .A(A13), .B(B13), .Output(Out13), .Cout(sumator_53_cout));
  Sumator sumator_57 (.Cin(sumator_53_cout), .A(A14), .B(B14), .Output(Out14), .Cout(sumator_57_cout));
  Sumator sumator_58 (.Cin(sumator_53_cout), .A(A14), .B(B14), .Output(Out14), .Cout(sumator_57_cout));
  Sumator sumator_59 (.Cin(sumator_53_cout), .A(A14), .B(B14), .Output(Out14), .Cout(sumator_57_cout));
  Sumator sumator_60 (.Cin(sumator_53_cout), .A(A14), .B(B14), .Output(Out14), .Cout(sumator_57_cout));
  Sumator sumator_61 (.Cin(sumator_53_cout), .A(A14), .B(B14), .Output(Out14), .Cout(sumator_57_cout));
  Sumator sumator_62 (.Cin(sumator_57_cout), .A(A15), .B(B15), .Output(Out15), .Cout(sumator_62_cout));
  Sumator sumator_63 (.Cin(sumator_57_cout), .A(A15), .B(B15), .Output(Out15), .Cout(sumator_62_cout));
  Sumator sumator_64 (.Cin(sumator_57_cout), .A(A15), .B(B15), .Output(Out15), .Cout(sumator_62_cout));
  Sumator sumator_65 (.Cin(sumator_57_cout), .A(A15), .B(B15), .Output(Out15), .Cout(sumator_62_cout));
  Sumator sumator_66 (.Cin(sumator_62_cout), .A(A16), .B(B16), .Output(Out16), .Cout(Out_cary));
  Sumator sumator_67 (.Cin(sumator_62_cout), .A(A16), .B(B16), .Output(Out16), .Cout(Out_cary));
  Sumator sumator_68 (.Cin(sumator_62_cout), .A(A16), .B(B16), .Output(Out16), .Cout(Out_cary));
  Sumator sumator_69 (.Cin(sumator_62_cout), .A(A16), .B(B16), .Output(Out16), .Cout(Out_cary));
endmodule
