// Digital circuit 1bit_registor.dig as structural Verilog
module _1bit_registor (
  input  Data1,
  input  Data2,
  input  Data3,
  input  Data4,
  input  Data5,
  input  Data6,
  input  Data7,
  input  Data8,
  input  Data9,
  input  Data10,
  input  Data11,
  input  Data12,
  input  Data13,
  input  Data14,
  input  Data15,
  input  Data16,
  input  ComA,
  input  ComB,
  input  Clock,
  input  DregComand,
  output OutA1,
  output OutA2,
  output OutA3,
  output OutA4,
  output OutA5,
  output OutA6,
  output OutA7,
  output OutA8,
  output OutA9,
  output OutA10,
  output OutA11,
  output OutA12,
  output OutA13,
  output OutA14,
  output OutA15,
  output OutA16,
  output OutB1,
  output OutB2,
  output OutB3,
  output OutB4,
  output OutB5,
  output OutB6,
  output OutB7,
  output OutB8,
  output OutB9,
  output OutB10,
  output OutB11,
  output OutB12,
  output OutB13,
  output OutB14,
  output OutB15,
  output OutB16
);

  wire and_1_out, d_triger_1_out, d_triger_2_out, d_triger_5_out, d_triger_8_out, d_triger_11_out,
       d_triger_14_out, d_triger_17_out, d_triger_20_out, d_triger_23_out, d_triger_26_out, d_triger_29_out,
       d_triger_32_out, d_triger_35_out, d_triger_38_out, d_triger_41_out, d_triger_44_out;

  d_triger d_triger_1 (.Data(Data1), .Clock(and_1_out), .out(d_triger_1_out));
  d_triger d_triger_2 (.Data(Data2), .Clock(and_1_out), .out(d_triger_2_out));
  d_triger d_triger_3 (.Data(Data2), .Clock(and_1_out), .out(d_triger_2_out));
  d_triger d_triger_4 (.Data(Data2), .Clock(and_1_out), .out(d_triger_2_out));
  d_triger d_triger_5 (.Data(Data3), .Clock(and_1_out), .out(d_triger_5_out));
  d_triger d_triger_6 (.Data(Data3), .Clock(and_1_out), .out(d_triger_5_out));
  d_triger d_triger_7 (.Data(Data3), .Clock(and_1_out), .out(d_triger_5_out));
  d_triger d_triger_8 (.Data(Data4), .Clock(and_1_out), .out(d_triger_8_out));
  d_triger d_triger_9 (.Data(Data4), .Clock(and_1_out), .out(d_triger_8_out));
  d_triger d_triger_10 (.Data(Data4), .Clock(and_1_out), .out(d_triger_8_out));
  d_triger d_triger_11 (.Data(Data5), .Clock(and_1_out), .out(d_triger_11_out));
  d_triger d_triger_12 (.Data(Data5), .Clock(and_1_out), .out(d_triger_11_out));
  d_triger d_triger_13 (.Data(Data5), .Clock(and_1_out), .out(d_triger_11_out));
  d_triger d_triger_14 (.Data(Data6), .Clock(and_1_out), .out(d_triger_14_out));
  d_triger d_triger_15 (.Data(Data6), .Clock(and_1_out), .out(d_triger_14_out));
  d_triger d_triger_16 (.Data(Data6), .Clock(and_1_out), .out(d_triger_14_out));
  d_triger d_triger_17 (.Data(Data7), .Clock(and_1_out), .out(d_triger_17_out));
  d_triger d_triger_18 (.Data(Data7), .Clock(and_1_out), .out(d_triger_17_out));
  d_triger d_triger_19 (.Data(Data7), .Clock(and_1_out), .out(d_triger_17_out));
  d_triger d_triger_20 (.Data(Data8), .Clock(and_1_out), .out(d_triger_20_out));
  d_triger d_triger_21 (.Data(Data8), .Clock(and_1_out), .out(d_triger_20_out));
  d_triger d_triger_22 (.Data(Data8), .Clock(and_1_out), .out(d_triger_20_out));
  d_triger d_triger_23 (.Data(Data9), .Clock(and_1_out), .out(d_triger_23_out));
  d_triger d_triger_24 (.Data(Data9), .Clock(and_1_out), .out(d_triger_23_out));
  d_triger d_triger_25 (.Data(Data9), .Clock(and_1_out), .out(d_triger_23_out));
  d_triger d_triger_26 (.Data(Data10), .Clock(and_1_out), .out(d_triger_26_out));
  d_triger d_triger_27 (.Data(Data10), .Clock(and_1_out), .out(d_triger_26_out));
  d_triger d_triger_28 (.Data(Data10), .Clock(and_1_out), .out(d_triger_26_out));
  d_triger d_triger_29 (.Data(Data11), .Clock(and_1_out), .out(d_triger_29_out));
  d_triger d_triger_30 (.Data(Data11), .Clock(and_1_out), .out(d_triger_29_out));
  d_triger d_triger_31 (.Data(Data11), .Clock(and_1_out), .out(d_triger_29_out));
  d_triger d_triger_32 (.Data(Data12), .Clock(and_1_out), .out(d_triger_32_out));
  d_triger d_triger_33 (.Data(Data12), .Clock(and_1_out), .out(d_triger_32_out));
  d_triger d_triger_34 (.Data(Data12), .Clock(and_1_out), .out(d_triger_32_out));
  d_triger d_triger_35 (.Data(Data13), .Clock(and_1_out), .out(d_triger_35_out));
  d_triger d_triger_36 (.Data(Data13), .Clock(and_1_out), .out(d_triger_35_out));
  d_triger d_triger_37 (.Data(Data13), .Clock(and_1_out), .out(d_triger_35_out));
  d_triger d_triger_38 (.Data(Data14), .Clock(and_1_out), .out(d_triger_38_out));
  d_triger d_triger_39 (.Data(Data14), .Clock(and_1_out), .out(d_triger_38_out));
  d_triger d_triger_40 (.Data(Data14), .Clock(and_1_out), .out(d_triger_38_out));
  d_triger d_triger_41 (.Data(Data15), .Clock(and_1_out), .out(d_triger_41_out));
  d_triger d_triger_42 (.Data(Data15), .Clock(and_1_out), .out(d_triger_41_out));
  d_triger d_triger_43 (.Data(Data15), .Clock(and_1_out), .out(d_triger_41_out));
  d_triger d_triger_44 (.Data(Data16), .Clock(and_1_out), .out(d_triger_44_out));
  d_triger d_triger_45 (.Data(Data16), .Clock(and_1_out), .out(d_triger_44_out));
  d_triger d_triger_46 (.Data(Data16), .Clock(and_1_out), .out(d_triger_44_out));
  and and_1 (and_1_out, DregComand, Clock);
  Tri_state_Buffer tri_state_buffer_1 (
    .ComA(ComA), .DataZbuffer(d_triger_1_out), .ComB(ComB), .DataA(OutB16), .DataB(OutA16));
  Tri_state_Buffer tri_state_buffer_2 (
    .ComA(ComA), .DataZbuffer(d_triger_2_out), .ComB(ComB), .DataA(OutB15), .DataB(OutA15));
  Tri_state_Buffer tri_state_buffer_3 (
    .ComA(ComA), .DataZbuffer(d_triger_5_out), .ComB(ComB), .DataA(OutB14), .DataB(OutA14));
  Tri_state_Buffer tri_state_buffer_4 (
    .ComA(ComA), .DataZbuffer(d_triger_8_out), .ComB(ComB), .DataA(OutB13), .DataB(OutA13));
  Tri_state_Buffer tri_state_buffer_5 (
    .ComA(ComA), .DataZbuffer(d_triger_11_out), .ComB(ComB), .DataA(OutB12), .DataB(OutA12));
  Tri_state_Buffer tri_state_buffer_6 (
    .ComA(ComA), .DataZbuffer(d_triger_14_out), .ComB(ComB), .DataA(OutB11), .DataB(OutA11));
  Tri_state_Buffer tri_state_buffer_7 (
    .ComA(ComA), .DataZbuffer(d_triger_17_out), .ComB(ComB), .DataA(OutB10), .DataB(OutA10));
  Tri_state_Buffer tri_state_buffer_8 (
    .ComA(ComA), .DataZbuffer(d_triger_20_out), .ComB(ComB), .DataA(OutB9), .DataB(OutA9));
  Tri_state_Buffer tri_state_buffer_9 (
    .ComA(ComA), .DataZbuffer(d_triger_23_out), .ComB(ComB), .DataA(OutB8), .DataB(OutA8));
  Tri_state_Buffer tri_state_buffer_10 (
    .ComA(ComA), .DataZbuffer(d_triger_26_out), .ComB(ComB), .DataA(OutB7), .DataB(OutA7));
  Tri_state_Buffer tri_state_buffer_11 (
    .ComA(ComA), .DataZbuffer(d_triger_29_out), .ComB(ComB), .DataA(OutB6), .DataB(OutA6));
  Tri_state_Buffer tri_state_buffer_12 (
    .ComA(ComA), .DataZbuffer(d_triger_32_out), .ComB(ComB), .DataA(OutB5), .DataB(OutA5));
  Tri_state_Buffer tri_state_buffer_13 (
    .ComA(ComA), .DataZbuffer(d_triger_35_out), .ComB(ComB), .DataA(OutB4), .DataB(OutA4));
  Tri_state_Buffer tri_state_buffer_14 (
    .ComA(ComA), .DataZbuffer(d_triger_38_out), .ComB(ComB), .DataA(OutB3), .DataB(OutA3));
  Tri_state_Buffer tri_state_buffer_15 (
    .ComA(ComA), .DataZbuffer(d_triger_41_out), .ComB(ComB), .DataA(OutB2), .DataB(OutA2));
  Tri_state_Buffer tri_state_buffer_16 (
    .ComA(ComA), .DataZbuffer(d_triger_44_out), .ComB(ComB), .DataA(OutB1), .DataB(OutA1));
endmodule
