// Digital circuit Tri-state Buffer.dig as structural Verilog
module Tri_state_Buffer (
  input  ComA,
  input  DataZbuffer,
  input  ComB,
  output DataA,
  output DataB
);

  assign DataA = ComA ? DataZbuffer : 1'bz;  // Driver driver_1
  assign DataB = ComB ? DataZbuffer : 1'bz;  // Driver driver_2
endmodule
