// Digital circuit d_triger.dig as structural Verilog
module d_triger (
  input  data,
  input  clock,
  output Q
);

  wire and_1_out, and_2_out, not_1_out, not_2_out, or_1_out, or_2_out;

  and and_1 (and_1_out, data, clock);
  and and_2 (and_2_out, clock, not_1_out);
  not not_1 (not_1_out, data);
  or or_1 (or_1_out, and_1_out, Q);
  or or_2 (or_2_out, not_2_out, and_2_out);
  not not_2 (not_2_out, or_1_out);
  not not_3 (Q, or_2_out);
endmodule
