// Digital circuit decoder.dig as structural Verilog
module decoder (
  input  B1main,
  input  B2,
  input  B3,
  input  B4,
  input  B5,
  input  B6,
  input  B7,
  input  B8,
  input  B9,
  input  B10,
  input  B11,
  input  B12,
  input  B13,
  input  B14,
  input  B15,
  input  B16,
  output Rout1,
  output Rout2,
  output Rout3,
  output Rout4,
  output Rout5,
  output Rout6,
  output Rout7,
  output Rout8,
  output Rb1,
  output Rb2,
  output Rb3,
  output Rb4,
  output Rb5,
  output Rb6,
  output Rb7,
  output Rb8,
  output Rb9,
  output Rb10,
  output Rb11,
  output Rb12,
  output Ra1,
  output Ra2,
  output Ra3,
  output Ra4,
  output Ra5,
  output Ra6,
  output Ra7,
  output Ra8,
  output Ra9,
  output Ra10,
  output Ra11,
  output Ra12,
  output plus,
  output out_50,
  output gt,
  output lt,
  output eq
);

  wire and_4_out, and_5_out, and_6_out, and_7_out, and_8_out, and_9_out, and_10_out, and_11_out, and_14_out,
       and_15_out, and_16_out, and_17_out, and_18_out, and_19_out, and_20_out, and_21_out, and_30_out,
       and_31_out, and_32_out, and_33_out, and_34_out, and_35_out, and_37_out, and_38_out, and_39_out,
       and_40_out, and_41_out, and_42_out, and_43_out, and_44_out, and_45_out, and_46_out, and_47_out,
       and_48_out, and_51_out, and_52_out, and_53_out, and_54_out, and_55_out, and_56_out, and_57_out,
       and_58_out, and_59_out, and_60_out, and_61_out, and_62_out, and_64_out, and_65_out, and_66_out,
       and_67_out, and_68_out, and_69_out, and_77_out, and_78_out, and_79_out, and_80_out, and_81_out,
       and_82_out, and_85_out, and_86_out, and_87_out, and_88_out, and_89_out, and_90_out, and_91_out,
       and_92_out, and_93_out, and_94_out, and_95_out, and_96_out, and_98_out, and_99_out, and_100_out,
       and_101_out, and_102_out, and_103_out, and_104_out, and_105_out, and_106_out, and_107_out,
       and_108_out, and_109_out, and_113_out, and_114_out, and_115_out, and_116_out, and_117_out,
       and_118_out, and_121_out, and_122_out, and_123_out, and_124_out, and_125_out, and_126_out,
       and_127_out, and_128_out, and_129_out, and_130_out, and_131_out, and_132_out, and_133_out,
       and_134_out, and_135_out, not_1_out, not_2_out, not_3_out, not_4_out, not_5_out, not_6_out, not_7_out,
       not_8_out, not_9_out, not_10_out, not_11_out, not_12_out, not_13_out, not_14_out, not_15_out,
       not_16_out, not_17_out, not_18_out, not_19_out, not_20_out, not_21_out, not_22_out, not_23_out,
       not_24_out, not_25_out, not_26_out, not_27_out, not_28_out, not_29_out, not_30_out, not_31_out,
       not_32_out, not_33_out, not_34_out, not_35_out, not_36_out, not_37_out, not_38_out, not_39_out,
       not_40_out, not_41_out, not_42_out, not_43_out, not_44_out, not_45_out, not_46_out, not_47_out,
       not_48_out, not_49_out, not_50_out, not_51_out, not_52_out, not_53_out, not_54_out, not_55_out,
       not_56_out, not_57_out, not_58_out, not_59_out, not_60_out, not_61_out, not_62_out, not_63_out,
       not_64_out, not_65_out, not_66_out, not_67_out, not_68_out, not_69_out, not_70_out, not_71_out,
       not_72_out, not_73_out, not_74_out, not_75_out, not_76_out, not_77_out, not_78_out;

  and and_1 (Rout8, B1main, and_14_out);
  and and_2 (Rout7, B1main, and_15_out);
  not not_1 (not_1_out, B14);
  not not_2 (not_2_out, B15);
  not not_3 (not_3_out, B15);
  not not_4 (not_4_out, B14);
  not not_5 (not_5_out, B16);
  not not_6 (not_6_out, B16);
  not not_7 (not_7_out, B14);
  not not_8 (not_8_out, B16);
  not not_9 (not_9_out, B15);
  not not_10 (not_10_out, B16);
  not not_11 (not_11_out, B15);
  not not_12 (not_12_out, B14);
  and and_3 (Rout6, B1main, and_16_out);
  and and_4 (and_4_out, B16, B15);
  and and_5 (and_5_out, B16, B15);
  and and_6 (and_6_out, B16, not_2_out);
  and and_7 (and_7_out, B16, not_3_out);
  and and_8 (and_8_out, not_5_out, B15);
  and and_9 (and_9_out, not_6_out, B15);
  and and_10 (and_10_out, not_8_out, not_9_out);
  and and_11 (and_11_out, not_10_out, not_11_out);
  and and_12 (Rout5, B1main, and_17_out);
  and and_13 (Rout4, B1main, and_18_out);
  and and_14 (and_14_out, and_4_out, B14);
  and and_15 (and_15_out, and_5_out, not_1_out);
  and and_16 (and_16_out, and_6_out, B14);
  and and_17 (and_17_out, and_7_out, not_4_out);
  and and_18 (and_18_out, and_8_out, B14);
  and and_19 (and_19_out, and_9_out, not_7_out);
  and and_20 (and_20_out, and_10_out, B14);
  and and_21 (and_21_out, and_11_out, not_12_out);
  and and_22 (Rout3, B1main, and_19_out);
  and and_23 (Rout2, B1main, and_20_out);
  and and_24 (Rout1, B1main, and_21_out);
  and and_25 (Rb12, and_30_out, B1main);
  and and_26 (Rb11, and_31_out, B1main);
  and and_27 (Rb10, and_32_out, B1main);
  and and_28 (Rb9, and_33_out, B1main);
  and and_29 (Rb8, and_34_out, B1main);
  and and_30 (and_30_out, and_38_out, and_37_out);
  and and_31 (and_31_out, and_40_out, and_39_out);
  and and_32 (and_32_out, and_42_out, and_41_out);
  and and_33 (and_33_out, and_44_out, and_43_out);
  and and_34 (and_34_out, and_46_out, and_45_out);
  and and_35 (and_35_out, and_48_out, and_47_out);
  and and_36 (Rb7, and_35_out, B1main);
  and and_37 (and_37_out, not_13_out, B13);
  and and_38 (and_38_out, B10, B11);
  and and_39 (and_39_out, not_14_out, B13);
  and and_40 (and_40_out, not_15_out, B11);
  and and_41 (and_41_out, not_16_out, B13);
  and and_42 (and_42_out, B10, not_17_out);
  and and_43 (and_43_out, not_18_out, B13);
  and and_44 (and_44_out, not_20_out, not_19_out);
  and and_45 (and_45_out, B12, not_21_out);
  and and_46 (and_46_out, B10, B11);
  and and_47 (and_47_out, B12, not_22_out);
  and and_48 (and_48_out, not_23_out, B11);
  not not_13 (not_13_out, B12);
  not not_14 (not_14_out, B12);
  not not_15 (not_15_out, B10);
  not not_16 (not_16_out, B12);
  not not_17 (not_17_out, B11);
  not not_18 (not_18_out, B12);
  not not_19 (not_19_out, B11);
  not not_20 (not_20_out, B10);
  not not_21 (not_21_out, B13);
  not not_22 (not_22_out, B13);
  not not_23 (not_23_out, B10);
  and and_49 (Rb6, B1main, and_64_out);
  not not_24 (not_24_out, B13);
  not not_25 (not_25_out, B11);
  not not_26 (not_26_out, B13);
  not not_27 (not_27_out, B11);
  not not_28 (not_28_out, B10);
  not not_29 (not_29_out, B13);
  not not_30 (not_30_out, B12);
  not not_31 (not_31_out, B13);
  not not_32 (not_32_out, B12);
  not not_33 (not_33_out, B10);
  not not_34 (not_34_out, B13);
  not not_35 (not_35_out, B12);
  not not_36 (not_36_out, B11);
  not not_37 (not_37_out, B13);
  not not_38 (not_38_out, B12);
  not not_39 (not_39_out, B11);
  not not_40 (not_40_out, B10);
  and and_50 (Rb5, B1main, and_65_out);
  and and_51 (and_51_out, not_24_out, B12);
  and and_52 (and_52_out, not_25_out, B10);
  and and_53 (and_53_out, not_26_out, B12);
  and and_54 (and_54_out, not_27_out, not_28_out);
  and and_55 (and_55_out, not_29_out, not_30_out);
  and and_56 (and_56_out, B11, B10);
  and and_57 (and_57_out, not_31_out, not_32_out);
  and and_58 (and_58_out, B11, not_33_out);
  and and_59 (and_59_out, not_34_out, not_35_out);
  and and_60 (and_60_out, not_36_out, B10);
  and and_61 (and_61_out, not_37_out, not_38_out);
  and and_62 (and_62_out, not_39_out, not_40_out);
  and and_63 (Rb4, B1main, and_66_out);
  and and_64 (and_64_out, and_51_out, and_52_out);
  and and_65 (and_65_out, and_53_out, and_54_out);
  and and_66 (and_66_out, and_55_out, and_56_out);
  and and_67 (and_67_out, and_57_out, and_58_out);
  and and_68 (and_68_out, and_59_out, and_60_out);
  and and_69 (and_69_out, and_61_out, and_62_out);
  and and_70 (Rb3, B1main, and_67_out);
  and and_71 (Rb2, B1main, and_68_out);
  and and_72 (Rb1, B1main, and_69_out);
  and and_73 (Ra12, and_82_out, B1main);
  and and_74 (Ra11, and_81_out, B1main);
  and and_75 (Ra10, and_80_out, B1main);
  and and_76 (Ra9, and_79_out, B1main);
  and and_77 (and_77_out, and_86_out, and_85_out);
  and and_78 (and_78_out, and_88_out, and_87_out);
  and and_79 (and_79_out, and_90_out, and_89_out);
  and and_80 (and_80_out, and_92_out, and_91_out);
  and and_81 (and_81_out, and_94_out, and_93_out);
  and and_82 (and_82_out, and_96_out, and_95_out);
  and and_83 (Ra8, and_78_out, B1main);
  and and_84 (Ra7, and_77_out, B1main);
  not not_41 (not_41_out, B8);
  and and_85 (and_85_out, not_41_out, B9);
  and and_86 (and_86_out, B6, B7);
  not not_42 (not_42_out, B8);
  and and_87 (and_87_out, not_42_out, B9);
  not not_43 (not_43_out, B6);
  and and_88 (and_88_out, not_43_out, B7);
  not not_44 (not_44_out, B8);
  and and_89 (and_89_out, not_44_out, B9);
  not not_45 (not_45_out, B7);
  and and_90 (and_90_out, B6, not_45_out);
  not not_46 (not_46_out, B8);
  and and_91 (and_91_out, not_46_out, B9);
  not not_47 (not_47_out, B7);
  not not_48 (not_48_out, B6);
  and and_92 (and_92_out, not_48_out, not_47_out);
  not not_49 (not_49_out, B9);
  and and_93 (and_93_out, B8, not_49_out);
  and and_94 (and_94_out, B6, B7);
  not not_50 (not_50_out, B9);
  and and_95 (and_95_out, B8, not_50_out);
  and and_96 (and_96_out, not_51_out, B7);
  not not_51 (not_51_out, B6);
  not not_52 (not_52_out, B9);
  not not_53 (not_53_out, B7);
  not not_54 (not_54_out, B9);
  not not_55 (not_55_out, B7);
  not not_56 (not_56_out, B6);
  not not_57 (not_57_out, B9);
  not not_58 (not_58_out, B8);
  not not_59 (not_59_out, B9);
  not not_60 (not_60_out, B8);
  not not_61 (not_61_out, B6);
  not not_62 (not_62_out, B9);
  not not_63 (not_63_out, B8);
  not not_64 (not_64_out, B7);
  not not_65 (not_65_out, B9);
  not not_66 (not_66_out, B8);
  not not_67 (not_67_out, B7);
  not not_68 (not_68_out, B6);
  and and_97 (Ra6, B1main, and_113_out);
  and and_98 (and_98_out, not_52_out, B8);
  and and_99 (and_99_out, not_53_out, B6);
  and and_100 (and_100_out, not_54_out, B8);
  and and_101 (and_101_out, not_55_out, not_56_out);
  and and_102 (and_102_out, not_57_out, not_58_out);
  and and_103 (and_103_out, B7, B6);
  and and_104 (and_104_out, not_59_out, not_60_out);
  and and_105 (and_105_out, B7, not_61_out);
  and and_106 (and_106_out, not_62_out, not_63_out);
  and and_107 (and_107_out, not_64_out, B6);
  and and_108 (and_108_out, not_65_out, not_66_out);
  and and_109 (and_109_out, not_67_out, not_68_out);
  and and_110 (Ra5, B1main, and_114_out);
  and and_111 (Ra4, B1main, and_115_out);
  and and_112 (Ra3, B1main, and_116_out);
  and and_113 (and_113_out, and_98_out, and_99_out);
  and and_114 (and_114_out, and_100_out, and_101_out);
  and and_115 (and_115_out, and_102_out, and_103_out);
  and and_116 (and_116_out, and_104_out, and_105_out);
  and and_117 (and_117_out, and_106_out, and_107_out);
  and and_118 (and_118_out, and_108_out, and_109_out);
  and and_119 (Ra2, B1main, and_117_out);
  and and_120 (Ra1, B1main, and_118_out);
  not not_69 (not_69_out, B4);
  not not_70 (not_70_out, B3);
  not not_71 (not_71_out, B5);
  not not_72 (not_72_out, B5);
  not not_73 (not_73_out, B3);
  not not_74 (not_74_out, B5);
  not not_75 (not_75_out, B4);
  not not_76 (not_76_out, B5);
  not not_77 (not_77_out, B4);
  not not_78 (not_78_out, B3);
  and and_121 (and_121_out, B5, not_69_out);
  and and_122 (and_122_out, not_71_out, B4);
  and and_123 (and_123_out, not_72_out, B4);
  and and_124 (and_124_out, not_74_out, not_75_out);
  and and_125 (and_125_out, not_76_out, not_77_out);
  and and_126 (and_126_out, and_121_out, not_70_out);
  and and_127 (and_127_out, and_122_out, B3);
  and and_128 (and_128_out, and_123_out, not_73_out);
  and and_129 (and_129_out, and_124_out, B3);
  and and_130 (and_130_out, and_125_out, not_78_out);
  and and_131 (and_131_out, B2, and_126_out);
  and and_132 (and_132_out, B2, and_127_out);
  and and_133 (and_133_out, B2, and_128_out);
  and and_134 (and_134_out, B2, and_129_out);
  and and_135 (and_135_out, B2, and_130_out);
  and and_136 (eq, and_131_out, B1main);
  and and_137 (lt, and_132_out, B1main);
  and and_138 (gt, and_133_out, B1main);
  and and_139 (out_50, and_134_out, B1main);
  and and_140 (plus, and_135_out, B1main);
endmodule
