// Digital circuit multiplexor.dig as structural Verilog
module multiplexor (
  input  Cin_com,
  input  CinA,
  output CoutA
);

  wire and_1_out, and_2_out, and_3_out, not_1_out, not_2_out, not_3_out, or_1_out;

  not not_1 (not_1_out, CinA);
  not not_2 (not_2_out, CinA);
  not not_3 (not_3_out, Cin_com);
  and and_1 (and_1_out, not_2_out, Cin_com);
  and and_2 (and_2_out, not_3_out, CinA);
  and and_3 (and_3_out, Cin_com, not_1_out);
  or or_1 (or_1_out, and_1_out, and_2_out);
  or or_2 (CoutA, or_1_out, and_3_out);
endmodule
