// Digital circuit procesor.dig as structural Verilog
module procesor (
  input  in_1,
  input  in_2,
  input  in_3,
  input  in_4,
  input  in_5,
  input  in_6,
  input  in_7,
  input  in_8,
  input  in_9,
  input  in_10,
  input  in_11,
  input  in_12,
  input  in_13,
  input  in_14,
  input  in_15,
  input  in_16,
  input  in_17,
  input  in_18,
  input  in_19,
  input  in_20,
  input  in_21,
  output out_22,
  output out_23,
  output out_24,
  output out_25
);

  wire _1bit_registor_1_outa1, _1bit_registor_1_outa2, _1bit_registor_1_outa3, _1bit_registor_1_outa4,
       _1bit_registor_1_outa5, _1bit_registor_1_outa6, _1bit_registor_1_outa7, _1bit_registor_1_outa8,
       _1bit_registor_1_outa9, _1bit_registor_1_outa10, _1bit_registor_1_outa11, _1bit_registor_1_outa12,
       _1bit_registor_1_outa13, _1bit_registor_1_outa14, _1bit_registor_1_outa15, _1bit_registor_1_outa16,
       _1bit_registor_1_outb1, _1bit_registor_1_outb2, _1bit_registor_1_outb3, _1bit_registor_1_outb4,
       _1bit_registor_1_outb5, _1bit_registor_1_outb6, _1bit_registor_1_outb7, _1bit_registor_1_outb8,
       _1bit_registor_1_outb9, _1bit_registor_1_outb10, _1bit_registor_1_outb11, _1bit_registor_1_outb12,
       _1bit_registor_1_outb13, _1bit_registor_1_outb14, _1bit_registor_1_outb15, _1bit_registor_1_outb16,
       _16bite_sumator_1_out1, _16bite_sumator_1_out2, _16bite_sumator_1_out3, _16bite_sumator_1_out4,
       _16bite_sumator_1_out5, _16bite_sumator_1_out6, _16bite_sumator_1_out7, _16bite_sumator_1_out8,
       _16bite_sumator_1_out9, _16bite_sumator_1_out10, _16bite_sumator_1_out11, _16bite_sumator_1_out12,
       _16bite_sumator_1_out13, _16bite_sumator_1_out14, _16bite_sumator_1_out15, _16bite_sumator_1_out16,
       _16bite_sumator_1_out_cary, decoder_1_plus, decoder_1_ra1, decoder_1_ra2, decoder_1_ra3,
       decoder_1_ra4, decoder_1_ra5, decoder_1_ra6, decoder_1_ra7, decoder_1_ra8, decoder_1_ra9,
       decoder_1_ra10, decoder_1_ra11, decoder_1_ra12, decoder_1_rb1, decoder_1_rb2, decoder_1_rb3,
       decoder_1_rb4, decoder_1_rb5, decoder_1_rb6, decoder_1_rb7, decoder_1_rb8, decoder_1_rb9,
       decoder_1_rb10, decoder_1_rb11, decoder_1_rb12, decoder_1_rout1, decoder_1_rout2, decoder_1_rout3,
       decoder_1_rout4, decoder_1_rout5, decoder_1_rout6, decoder_1_rout7, decoder_1_rout8, driver_1_out,
       driver_2_out, driver_3_out, driver_4_out, driver_5_out, driver_6_out, driver_7_out, driver_8_out,
       driver_9_out, driver_10_out, driver_11_out, driver_12_out, driver_13_out, driver_14_out,
       driver_15_out, driver_16_out, multiplexor_1_couta, multiplexor_2_couta, multiplexor_3_couta,
       multiplexor_4_couta, multiplexor_5_couta, multiplexor_6_couta, multiplexor_7_couta,
       multiplexor_8_couta, multiplexor_9_couta, multiplexor_10_couta, multiplexor_11_couta,
       multiplexor_12_couta, multiplexor_13_couta, multiplexor_14_couta, multiplexor_15_couta,
       multiplexor_16_couta;

  decoder decoder_1 (
    .B1main(in_1), .B2(in_2), .B3(in_3), .B4(in_21), .B5(in_4), .B6(in_5), .B7(in_6), .B8(in_7), .B9(in_8),
    .B10(in_9), .B11(in_10), .B12(in_11), .B13(in_12), .B14(in_13), .B15(in_14), .B16(in_15),
    .Rout1(decoder_1_rout1), .Rout2(decoder_1_rout2), .Rout3(decoder_1_rout3), .Rout4(decoder_1_rout4),
    .Rout5(decoder_1_rout5), .Rout6(decoder_1_rout6), .Rout7(decoder_1_rout7), .Rout8(decoder_1_rout8),
    .Rb1(decoder_1_rb1), .Rb2(decoder_1_rb2), .Rb3(decoder_1_rb3), .Rb4(decoder_1_rb4), .Rb5(decoder_1_rb5),
    .Rb6(decoder_1_rb6), .Rb7(decoder_1_rb7), .Rb8(decoder_1_rb8), .Rb9(decoder_1_rb9),
    .Rb10(decoder_1_rb10), .Rb11(decoder_1_rb11), .Rb12(decoder_1_rb12), .Ra1(decoder_1_ra1),
    .Ra2(decoder_1_ra2), .Ra3(decoder_1_ra3), .Ra4(decoder_1_ra4), .Ra5(decoder_1_ra5), .Ra6(decoder_1_ra6),
    .Ra7(decoder_1_ra7), .Ra8(decoder_1_ra8), .Ra9(decoder_1_ra9), .Ra10(decoder_1_ra10),
    .Ra11(decoder_1_ra11), .Ra12(decoder_1_ra12), .plus(decoder_1_plus), .out_50(out_25), .gt(out_24),
    .lt(out_23), .eq(out_22));
  _1bit_registor _1bit_registor_1 (
    .Data1(driver_15_out), .Data2(driver_16_out), .Data3(driver_13_out), .Data4(driver_14_out),
    .Data5(driver_11_out), .Data6(driver_12_out), .Data7(driver_9_out), .Data8(driver_10_out),
    .Data9(driver_7_out), .Data10(driver_8_out), .Data11(driver_5_out), .Data12(driver_6_out),
    .Data13(driver_3_out), .Data14(driver_4_out), .Data15(driver_1_out), .Data16(driver_2_out),
    .ComA(decoder_1_ra1), .ComB(decoder_1_rb1), .Clock(in_20), .DregComand(decoder_1_rout1),
    .OutA1(_1bit_registor_1_outa1), .OutA2(_1bit_registor_1_outa2), .OutA3(_1bit_registor_1_outa3),
    .OutA4(_1bit_registor_1_outa4), .OutA5(_1bit_registor_1_outa5), .OutA6(_1bit_registor_1_outa6),
    .OutA7(_1bit_registor_1_outa7), .OutA8(_1bit_registor_1_outa8), .OutA9(_1bit_registor_1_outa9),
    .OutA10(_1bit_registor_1_outa10), .OutA11(_1bit_registor_1_outa11), .OutA12(_1bit_registor_1_outa12),
    .OutA13(_1bit_registor_1_outa13), .OutA14(_1bit_registor_1_outa14), .OutA15(_1bit_registor_1_outa15),
    .OutA16(_1bit_registor_1_outa16), .OutB1(_1bit_registor_1_outb1), .OutB2(_1bit_registor_1_outb2),
    .OutB3(_1bit_registor_1_outb3), .OutB4(_1bit_registor_1_outb4), .OutB5(_1bit_registor_1_outb5),
    .OutB6(_1bit_registor_1_outb6), .OutB7(_1bit_registor_1_outb7), .OutB8(_1bit_registor_1_outb8),
    .OutB9(_1bit_registor_1_outb9), .OutB10(_1bit_registor_1_outb10), .OutB11(_1bit_registor_1_outb11),
    .OutB12(_1bit_registor_1_outb12), .OutB13(_1bit_registor_1_outb13), .OutB14(_1bit_registor_1_outb14),
    .OutB15(_1bit_registor_1_outb15), .OutB16(_1bit_registor_1_outb16));
  _1bit_registor _1bit_registor_2 (
    .Data1(driver_15_out), .Data2(driver_16_out), .Data3(driver_13_out), .Data4(driver_14_out),
    .Data5(driver_11_out), .Data6(driver_12_out), .Data7(driver_9_out), .Data8(driver_10_out),
    .Data9(driver_7_out), .Data10(driver_8_out), .Data11(driver_5_out), .Data12(driver_6_out),
    .Data13(driver_3_out), .Data14(driver_4_out), .Data15(driver_1_out), .Data16(driver_2_out),
    .ComA(decoder_1_ra2), .ComB(decoder_1_rb2), .Clock(in_20), .DregComand(decoder_1_rout2),
    .OutA1(_1bit_registor_1_outa1), .OutA2(_1bit_registor_1_outa2), .OutA3(_1bit_registor_1_outa3),
    .OutA4(_1bit_registor_1_outa4), .OutA5(_1bit_registor_1_outa5), .OutA6(_1bit_registor_1_outa6),
    .OutA7(_1bit_registor_1_outa7), .OutA8(_1bit_registor_1_outa8), .OutA9(_1bit_registor_1_outa9),
    .OutA10(_1bit_registor_1_outa10), .OutA11(_1bit_registor_1_outa11), .OutA12(_1bit_registor_1_outa12),
    .OutA13(_1bit_registor_1_outa13), .OutA14(_1bit_registor_1_outa14), .OutA15(_1bit_registor_1_outa15),
    .OutA16(_1bit_registor_1_outa16), .OutB1(_1bit_registor_1_outb1), .OutB2(_1bit_registor_1_outb2),
    .OutB3(_1bit_registor_1_outb3), .OutB4(_1bit_registor_1_outb4), .OutB5(_1bit_registor_1_outb5),
    .OutB6(_1bit_registor_1_outb6), .OutB7(_1bit_registor_1_outb7), .OutB8(_1bit_registor_1_outb8),
    .OutB9(_1bit_registor_1_outb9), .OutB10(_1bit_registor_1_outb10), .OutB11(_1bit_registor_1_outb11),
    .OutB12(_1bit_registor_1_outb12), .OutB13(_1bit_registor_1_outb13), .OutB14(_1bit_registor_1_outb14),
    .OutB15(_1bit_registor_1_outb15), .OutB16(_1bit_registor_1_outb16));
  _1bit_registor _1bit_registor_3 (
    .Data1(driver_15_out), .Data2(driver_16_out), .Data3(driver_13_out), .Data4(driver_14_out),
    .Data5(driver_11_out), .Data6(driver_12_out), .Data7(driver_9_out), .Data8(driver_10_out),
    .Data9(driver_7_out), .Data10(driver_8_out), .Data11(driver_5_out), .Data12(driver_6_out),
    .Data13(driver_3_out), .Data14(driver_4_out), .Data15(driver_1_out), .Data16(driver_2_out),
    .ComA(decoder_1_ra7), .ComB(decoder_1_rb7), .Clock(in_20), .DregComand(decoder_1_rout7),
    .OutA1(_1bit_registor_1_outa1), .OutA2(_1bit_registor_1_outa2), .OutA3(_1bit_registor_1_outa3),
    .OutA4(_1bit_registor_1_outa4), .OutA5(_1bit_registor_1_outa5), .OutA6(_1bit_registor_1_outa6),
    .OutA7(_1bit_registor_1_outa7), .OutA8(_1bit_registor_1_outa8), .OutA9(_1bit_registor_1_outa9),
    .OutA10(_1bit_registor_1_outa10), .OutA11(_1bit_registor_1_outa11), .OutA12(_1bit_registor_1_outa12),
    .OutA13(_1bit_registor_1_outa13), .OutA14(_1bit_registor_1_outa14), .OutA15(_1bit_registor_1_outa15),
    .OutA16(_1bit_registor_1_outa16), .OutB1(_1bit_registor_1_outb1), .OutB2(_1bit_registor_1_outb2),
    .OutB3(_1bit_registor_1_outb3), .OutB4(_1bit_registor_1_outb4), .OutB5(_1bit_registor_1_outb5),
    .OutB6(_1bit_registor_1_outb6), .OutB7(_1bit_registor_1_outb7), .OutB8(_1bit_registor_1_outb8),
    .OutB9(_1bit_registor_1_outb9), .OutB10(_1bit_registor_1_outb10), .OutB11(_1bit_registor_1_outb11),
    .OutB12(_1bit_registor_1_outb12), .OutB13(_1bit_registor_1_outb13), .OutB14(_1bit_registor_1_outb14),
    .OutB15(_1bit_registor_1_outb15), .OutB16(_1bit_registor_1_outb16));
  _1bit_registor _1bit_registor_4 (
    .Data1(driver_15_out), .Data2(driver_16_out), .Data3(driver_13_out), .Data4(driver_14_out),
    .Data5(driver_11_out), .Data6(driver_12_out), .Data7(driver_9_out), .Data8(driver_10_out),
    .Data9(driver_7_out), .Data10(driver_8_out), .Data11(driver_5_out), .Data12(driver_6_out),
    .Data13(driver_3_out), .Data14(driver_4_out), .Data15(driver_1_out), .Data16(driver_2_out),
    .ComA(decoder_1_ra3), .ComB(decoder_1_rb3), .Clock(in_20), .DregComand(decoder_1_rout3),
    .OutA1(_1bit_registor_1_outa1), .OutA2(_1bit_registor_1_outa2), .OutA3(_1bit_registor_1_outa3),
    .OutA4(_1bit_registor_1_outa4), .OutA5(_1bit_registor_1_outa5), .OutA6(_1bit_registor_1_outa6),
    .OutA7(_1bit_registor_1_outa7), .OutA8(_1bit_registor_1_outa8), .OutA9(_1bit_registor_1_outa9),
    .OutA10(_1bit_registor_1_outa10), .OutA11(_1bit_registor_1_outa11), .OutA12(_1bit_registor_1_outa12),
    .OutA13(_1bit_registor_1_outa13), .OutA14(_1bit_registor_1_outa14), .OutA15(_1bit_registor_1_outa15),
    .OutA16(_1bit_registor_1_outa16), .OutB1(_1bit_registor_1_outb1), .OutB2(_1bit_registor_1_outb2),
    .OutB3(_1bit_registor_1_outb3), .OutB4(_1bit_registor_1_outb4), .OutB5(_1bit_registor_1_outb5),
    .OutB6(_1bit_registor_1_outb6), .OutB7(_1bit_registor_1_outb7), .OutB8(_1bit_registor_1_outb8),
    .OutB9(_1bit_registor_1_outb9), .OutB10(_1bit_registor_1_outb10), .OutB11(_1bit_registor_1_outb11),
    .OutB12(_1bit_registor_1_outb12), .OutB13(_1bit_registor_1_outb13), .OutB14(_1bit_registor_1_outb14),
    .OutB15(_1bit_registor_1_outb15), .OutB16(_1bit_registor_1_outb16));
  _1bit_registor _1bit_registor_5 (
    .Data1(driver_15_out), .Data2(driver_16_out), .Data3(driver_13_out), .Data4(driver_14_out),
    .Data5(driver_11_out), .Data6(driver_12_out), .Data7(driver_9_out), .Data8(driver_10_out),
    .Data9(driver_7_out), .Data10(driver_8_out), .Data11(driver_5_out), .Data12(driver_6_out),
    .Data13(driver_3_out), .Data14(driver_4_out), .Data15(driver_1_out), .Data16(driver_2_out),
    .ComA(decoder_1_ra8), .ComB(decoder_1_rb8), .Clock(in_20), .DregComand(decoder_1_rout8),
    .OutA1(_1bit_registor_1_outa1), .OutA2(_1bit_registor_1_outa2), .OutA3(_1bit_registor_1_outa3),
    .OutA4(_1bit_registor_1_outa4), .OutA5(_1bit_registor_1_outa5), .OutA6(_1bit_registor_1_outa6),
    .OutA7(_1bit_registor_1_outa7), .OutA8(_1bit_registor_1_outa8), .OutA9(_1bit_registor_1_outa9),
    .OutA10(_1bit_registor_1_outa10), .OutA11(_1bit_registor_1_outa11), .OutA12(_1bit_registor_1_outa12),
    .OutA13(_1bit_registor_1_outa13), .OutA14(_1bit_registor_1_outa14), .OutA15(_1bit_registor_1_outa15),
    .OutA16(_1bit_registor_1_outa16), .OutB1(_1bit_registor_1_outb1), .OutB2(_1bit_registor_1_outb2),
    .OutB3(_1bit_registor_1_outb3), .OutB4(_1bit_registor_1_outb4), .OutB5(_1bit_registor_1_outb5),
    .OutB6(_1bit_registor_1_outb6), .OutB7(_1bit_registor_1_outb7), .OutB8(_1bit_registor_1_outb8),
    .OutB9(_1bit_registor_1_outb9), .OutB10(_1bit_registor_1_outb10), .OutB11(_1bit_registor_1_outb11),
    .OutB12(_1bit_registor_1_outb12), .OutB13(_1bit_registor_1_outb13), .OutB14(_1bit_registor_1_outb14),
    .OutB15(_1bit_registor_1_outb15), .OutB16(_1bit_registor_1_outb16));
  _1bit_registor _1bit_registor_6 (
    .Data1(driver_15_out), .Data2(driver_16_out), .Data3(driver_13_out), .Data4(driver_14_out),
    .Data5(driver_11_out), .Data6(driver_12_out), .Data7(driver_9_out), .Data8(driver_10_out),
    .Data9(driver_7_out), .Data10(driver_8_out), .Data11(driver_5_out), .Data12(driver_6_out),
    .Data13(driver_3_out), .Data14(driver_4_out), .Data15(driver_1_out), .Data16(driver_2_out),
    .ComA(decoder_1_ra9), .ComB(decoder_1_rb9), .Clock(in_20), .DregComand(in_16),
    .OutA1(_1bit_registor_1_outa1), .OutA2(_1bit_registor_1_outa2), .OutA3(_1bit_registor_1_outa3),
    .OutA4(_1bit_registor_1_outa4), .OutA5(_1bit_registor_1_outa5), .OutA6(_1bit_registor_1_outa6),
    .OutA7(_1bit_registor_1_outa7), .OutA8(_1bit_registor_1_outa8), .OutA9(_1bit_registor_1_outa9),
    .OutA10(_1bit_registor_1_outa10), .OutA11(_1bit_registor_1_outa11), .OutA12(_1bit_registor_1_outa12),
    .OutA13(_1bit_registor_1_outa13), .OutA14(_1bit_registor_1_outa14), .OutA15(_1bit_registor_1_outa15),
    .OutA16(_1bit_registor_1_outa16), .OutB1(_1bit_registor_1_outb1), .OutB2(_1bit_registor_1_outb2),
    .OutB3(_1bit_registor_1_outb3), .OutB4(_1bit_registor_1_outb4), .OutB5(_1bit_registor_1_outb5),
    .OutB6(_1bit_registor_1_outb6), .OutB7(_1bit_registor_1_outb7), .OutB8(_1bit_registor_1_outb8),
    .OutB9(_1bit_registor_1_outb9), .OutB10(_1bit_registor_1_outb10), .OutB11(_1bit_registor_1_outb11),
    .OutB12(_1bit_registor_1_outb12), .OutB13(_1bit_registor_1_outb13), .OutB14(_1bit_registor_1_outb14),
    .OutB15(_1bit_registor_1_outb15), .OutB16(_1bit_registor_1_outb16));
  _1bit_registor _1bit_registor_7 (
    .Data1(driver_15_out), .Data2(driver_16_out), .Data3(driver_13_out), .Data4(driver_14_out),
    .Data5(driver_11_out), .Data6(driver_12_out), .Data7(driver_9_out), .Data8(driver_10_out),
    .Data9(driver_7_out), .Data10(driver_8_out), .Data11(driver_5_out), .Data12(driver_6_out),
    .Data13(driver_3_out), .Data14(driver_4_out), .Data15(driver_1_out), .Data16(driver_2_out),
    .ComA(decoder_1_ra4), .ComB(decoder_1_rb4), .Clock(in_20), .DregComand(decoder_1_rout4),
    .OutA1(_1bit_registor_1_outa1), .OutA2(_1bit_registor_1_outa2), .OutA3(_1bit_registor_1_outa3),
    .OutA4(_1bit_registor_1_outa4), .OutA5(_1bit_registor_1_outa5), .OutA6(_1bit_registor_1_outa6),
    .OutA7(_1bit_registor_1_outa7), .OutA8(_1bit_registor_1_outa8), .OutA9(_1bit_registor_1_outa9),
    .OutA10(_1bit_registor_1_outa10), .OutA11(_1bit_registor_1_outa11), .OutA12(_1bit_registor_1_outa12),
    .OutA13(_1bit_registor_1_outa13), .OutA14(_1bit_registor_1_outa14), .OutA15(_1bit_registor_1_outa15),
    .OutA16(_1bit_registor_1_outa16), .OutB1(_1bit_registor_1_outb1), .OutB2(_1bit_registor_1_outb2),
    .OutB3(_1bit_registor_1_outb3), .OutB4(_1bit_registor_1_outb4), .OutB5(_1bit_registor_1_outb5),
    .OutB6(_1bit_registor_1_outb6), .OutB7(_1bit_registor_1_outb7), .OutB8(_1bit_registor_1_outb8),
    .OutB9(_1bit_registor_1_outb9), .OutB10(_1bit_registor_1_outb10), .OutB11(_1bit_registor_1_outb11),
    .OutB12(_1bit_registor_1_outb12), .OutB13(_1bit_registor_1_outb13), .OutB14(_1bit_registor_1_outb14),
    .OutB15(_1bit_registor_1_outb15), .OutB16(_1bit_registor_1_outb16));
  _1bit_registor _1bit_registor_8 (
    .Data1(driver_15_out), .Data2(driver_16_out), .Data3(driver_13_out), .Data4(driver_14_out),
    .Data5(driver_11_out), .Data6(driver_12_out), .Data7(driver_9_out), .Data8(driver_10_out),
    .Data9(driver_7_out), .Data10(driver_8_out), .Data11(driver_5_out), .Data12(driver_6_out),
    .Data13(driver_3_out), .Data14(driver_4_out), .Data15(driver_1_out), .Data16(driver_2_out),
    .ComA(decoder_1_ra10), .ComB(decoder_1_rb10), .Clock(in_20), .DregComand(in_17),
    .OutA1(_1bit_registor_1_outa1), .OutA2(_1bit_registor_1_outa2), .OutA3(_1bit_registor_1_outa3),
    .OutA4(_1bit_registor_1_outa4), .OutA5(_1bit_registor_1_outa5), .OutA6(_1bit_registor_1_outa6),
    .OutA7(_1bit_registor_1_outa7), .OutA8(_1bit_registor_1_outa8), .OutA9(_1bit_registor_1_outa9),
    .OutA10(_1bit_registor_1_outa10), .OutA11(_1bit_registor_1_outa11), .OutA12(_1bit_registor_1_outa12),
    .OutA13(_1bit_registor_1_outa13), .OutA14(_1bit_registor_1_outa14), .OutA15(_1bit_registor_1_outa15),
    .OutA16(_1bit_registor_1_outa16), .OutB1(_1bit_registor_1_outb1), .OutB2(_1bit_registor_1_outb2),
    .OutB3(_1bit_registor_1_outb3), .OutB4(_1bit_registor_1_outb4), .OutB5(_1bit_registor_1_outb5),
    .OutB6(_1bit_registor_1_outb6), .OutB7(_1bit_registor_1_outb7), .OutB8(_1bit_registor_1_outb8),
    .OutB9(_1bit_registor_1_outb9), .OutB10(_1bit_registor_1_outb10), .OutB11(_1bit_registor_1_outb11),
    .OutB12(_1bit_registor_1_outb12), .OutB13(_1bit_registor_1_outb13), .OutB14(_1bit_registor_1_outb14),
    .OutB15(_1bit_registor_1_outb15), .OutB16(_1bit_registor_1_outb16));
  _1bit_registor _1bit_registor_9 (
    .Data1(driver_15_out), .Data2(driver_16_out), .Data3(driver_13_out), .Data4(driver_14_out),
    .Data5(driver_11_out), .Data6(driver_12_out), .Data7(driver_9_out), .Data8(driver_10_out),
    .Data9(driver_7_out), .Data10(driver_8_out), .Data11(driver_5_out), .Data12(driver_6_out),
    .Data13(driver_3_out), .Data14(driver_4_out), .Data15(driver_1_out), .Data16(driver_2_out),
    .ComA(decoder_1_ra5), .ComB(decoder_1_rb5), .Clock(in_20), .DregComand(decoder_1_rout5),
    .OutA1(_1bit_registor_1_outa1), .OutA2(_1bit_registor_1_outa2), .OutA3(_1bit_registor_1_outa3),
    .OutA4(_1bit_registor_1_outa4), .OutA5(_1bit_registor_1_outa5), .OutA6(_1bit_registor_1_outa6),
    .OutA7(_1bit_registor_1_outa7), .OutA8(_1bit_registor_1_outa8), .OutA9(_1bit_registor_1_outa9),
    .OutA10(_1bit_registor_1_outa10), .OutA11(_1bit_registor_1_outa11), .OutA12(_1bit_registor_1_outa12),
    .OutA13(_1bit_registor_1_outa13), .OutA14(_1bit_registor_1_outa14), .OutA15(_1bit_registor_1_outa15),
    .OutA16(_1bit_registor_1_outa16), .OutB1(_1bit_registor_1_outb1), .OutB2(_1bit_registor_1_outb2),
    .OutB3(_1bit_registor_1_outb3), .OutB4(_1bit_registor_1_outb4), .OutB5(_1bit_registor_1_outb5),
    .OutB6(_1bit_registor_1_outb6), .OutB7(_1bit_registor_1_outb7), .OutB8(_1bit_registor_1_outb8),
    .OutB9(_1bit_registor_1_outb9), .OutB10(_1bit_registor_1_outb10), .OutB11(_1bit_registor_1_outb11),
    .OutB12(_1bit_registor_1_outb12), .OutB13(_1bit_registor_1_outb13), .OutB14(_1bit_registor_1_outb14),
    .OutB15(_1bit_registor_1_outb15), .OutB16(_1bit_registor_1_outb16));
  _1bit_registor _1bit_registor_10 (
    .Data1(driver_15_out), .Data2(driver_16_out), .Data3(driver_13_out), .Data4(driver_14_out),
    .Data5(driver_11_out), .Data6(driver_12_out), .Data7(driver_9_out), .Data8(driver_10_out),
    .Data9(driver_7_out), .Data10(driver_8_out), .Data11(driver_5_out), .Data12(driver_6_out),
    .Data13(driver_3_out), .Data14(driver_4_out), .Data15(driver_1_out), .Data16(driver_2_out),
    .ComA(decoder_1_ra6), .ComB(decoder_1_rb6), .Clock(in_20), .DregComand(decoder_1_rout6),
    .OutA1(_1bit_registor_1_outa1), .OutA2(_1bit_registor_1_outa2), .OutA3(_1bit_registor_1_outa3),
    .OutA4(_1bit_registor_1_outa4), .OutA5(_1bit_registor_1_outa5), .OutA6(_1bit_registor_1_outa6),
    .OutA7(_1bit_registor_1_outa7), .OutA8(_1bit_registor_1_outa8), .OutA9(_1bit_registor_1_outa9),
    .OutA10(_1bit_registor_1_outa10), .OutA11(_1bit_registor_1_outa11), .OutA12(_1bit_registor_1_outa12),
    .OutA13(_1bit_registor_1_outa13), .OutA14(_1bit_registor_1_outa14), .OutA15(_1bit_registor_1_outa15),
    .OutA16(_1bit_registor_1_outa16), .OutB1(_1bit_registor_1_outb1), .OutB2(_1bit_registor_1_outb2),
    .OutB3(_1bit_registor_1_outb3), .OutB4(_1bit_registor_1_outb4), .OutB5(_1bit_registor_1_outb5),
    .OutB6(_1bit_registor_1_outb6), .OutB7(_1bit_registor_1_outb7), .OutB8(_1bit_registor_1_outb8),
    .OutB9(_1bit_registor_1_outb9), .OutB10(_1bit_registor_1_outb10), .OutB11(_1bit_registor_1_outb11),
    .OutB12(_1bit_registor_1_outb12), .OutB13(_1bit_registor_1_outb13), .OutB14(_1bit_registor_1_outb14),
    .OutB15(_1bit_registor_1_outb15), .OutB16(_1bit_registor_1_outb16));
  _1bit_registor _1bit_registor_11 (
    .Data1(driver_15_out), .Data2(driver_16_out), .Data3(driver_13_out), .Data4(driver_14_out),
    .Data5(driver_11_out), .Data6(driver_12_out), .Data7(driver_9_out), .Data8(driver_10_out),
    .Data9(driver_7_out), .Data10(driver_8_out), .Data11(driver_5_out), .Data12(driver_6_out),
    .Data13(driver_3_out), .Data14(driver_4_out), .Data15(driver_1_out), .Data16(driver_2_out),
    .ComA(decoder_1_ra11), .ComB(decoder_1_rb11), .Clock(in_20), .DregComand(in_18),
    .OutA1(_1bit_registor_1_outa1), .OutA2(_1bit_registor_1_outa2), .OutA3(_1bit_registor_1_outa3),
    .OutA4(_1bit_registor_1_outa4), .OutA5(_1bit_registor_1_outa5), .OutA6(_1bit_registor_1_outa6),
    .OutA7(_1bit_registor_1_outa7), .OutA8(_1bit_registor_1_outa8), .OutA9(_1bit_registor_1_outa9),
    .OutA10(_1bit_registor_1_outa10), .OutA11(_1bit_registor_1_outa11), .OutA12(_1bit_registor_1_outa12),
    .OutA13(_1bit_registor_1_outa13), .OutA14(_1bit_registor_1_outa14), .OutA15(_1bit_registor_1_outa15),
    .OutA16(_1bit_registor_1_outa16), .OutB1(_1bit_registor_1_outb1), .OutB2(_1bit_registor_1_outb2),
    .OutB3(_1bit_registor_1_outb3), .OutB4(_1bit_registor_1_outb4), .OutB5(_1bit_registor_1_outb5),
    .OutB6(_1bit_registor_1_outb6), .OutB7(_1bit_registor_1_outb7), .OutB8(_1bit_registor_1_outb8),
    .OutB9(_1bit_registor_1_outb9), .OutB10(_1bit_registor_1_outb10), .OutB11(_1bit_registor_1_outb11),
    .OutB12(_1bit_registor_1_outb12), .OutB13(_1bit_registor_1_outb13), .OutB14(_1bit_registor_1_outb14),
    .OutB15(_1bit_registor_1_outb15), .OutB16(_1bit_registor_1_outb16));
  multiplexor multiplexor_1 (.CinA(_1bit_registor_1_outa9), .Cin_com(decoder_1_plus), .CoutA(multiplexor_1_couta));
  multiplexor multiplexor_2 (.CinA(_1bit_registor_1_outa10), .Cin_com(decoder_1_plus), .CoutA(multiplexor_2_couta));
  multiplexor multiplexor_3 (.CinA(_1bit_registor_1_outa11), .Cin_com(decoder_1_plus), .CoutA(multiplexor_3_couta));
  multiplexor multiplexor_4 (.CinA(_1bit_registor_1_outa12), .Cin_com(decoder_1_plus), .CoutA(multiplexor_4_couta));
  multiplexor multiplexor_5 (.CinA(_1bit_registor_1_outa13), .Cin_com(decoder_1_plus), .CoutA(multiplexor_5_couta));
  multiplexor multiplexor_6 (.CinA(_1bit_registor_1_outa14), .Cin_com(decoder_1_plus), .CoutA(multiplexor_6_couta));
  multiplexor multiplexor_7 (.CinA(_1bit_registor_1_outa15), .Cin_com(decoder_1_plus), .CoutA(multiplexor_7_couta));
  multiplexor multiplexor_8 (.CinA(_1bit_registor_1_outa16), .Cin_com(decoder_1_plus), .CoutA(multiplexor_8_couta));
  multiplexor multiplexor_9 (.CinA(_1bit_registor_1_outa1), .Cin_com(decoder_1_plus), .CoutA(multiplexor_9_couta));
  multiplexor multiplexor_10 (.CinA(_1bit_registor_1_outa2), .Cin_com(decoder_1_plus), .CoutA(multiplexor_10_couta));
  multiplexor multiplexor_11 (.CinA(_1bit_registor_1_outa3), .Cin_com(decoder_1_plus), .CoutA(multiplexor_11_couta));
  multiplexor multiplexor_12 (.CinA(_1bit_registor_1_outa4), .Cin_com(decoder_1_plus), .CoutA(multiplexor_12_couta));
  multiplexor multiplexor_13 (.CinA(_1bit_registor_1_outa5), .Cin_com(decoder_1_plus), .CoutA(multiplexor_13_couta));
  multiplexor multiplexor_14 (.CinA(_1bit_registor_1_outa6), .Cin_com(decoder_1_plus), .CoutA(multiplexor_14_couta));
  multiplexor multiplexor_15 (.CinA(_1bit_registor_1_outa7), .Cin_com(decoder_1_plus), .CoutA(multiplexor_15_couta));
  multiplexor multiplexor_16 (.CinA(_1bit_registor_1_outa8), .Cin_com(decoder_1_plus), .CoutA(multiplexor_16_couta));
  _1bit_registor _1bit_registor_12 (
    .Data1(driver_15_out), .Data2(driver_16_out), .Data3(driver_13_out), .Data4(driver_14_out),
    .Data5(driver_11_out), .Data6(driver_12_out), .Data7(driver_9_out), .Data8(driver_10_out),
    .Data9(driver_7_out), .Data10(driver_8_out), .Data11(driver_5_out), .Data12(driver_6_out),
    .Data13(driver_3_out), .Data14(driver_4_out), .Data15(driver_1_out), .Data16(driver_2_out),
    .ComA(decoder_1_ra12), .ComB(decoder_1_rb12), .Clock(in_20), .DregComand(in_19),
    .OutA1(_1bit_registor_1_outa1), .OutA2(_1bit_registor_1_outa2), .OutA3(_1bit_registor_1_outa3),
    .OutA4(_1bit_registor_1_outa4), .OutA5(_1bit_registor_1_outa5), .OutA6(_1bit_registor_1_outa6),
    .OutA7(_1bit_registor_1_outa7), .OutA8(_1bit_registor_1_outa8), .OutA9(_1bit_registor_1_outa9),
    .OutA10(_1bit_registor_1_outa10), .OutA11(_1bit_registor_1_outa11), .OutA12(_1bit_registor_1_outa12),
    .OutA13(_1bit_registor_1_outa13), .OutA14(_1bit_registor_1_outa14), .OutA15(_1bit_registor_1_outa15),
    .OutA16(_1bit_registor_1_outa16), .OutB1(_1bit_registor_1_outb1), .OutB2(_1bit_registor_1_outb2),
    .OutB3(_1bit_registor_1_outb3), .OutB4(_1bit_registor_1_outb4), .OutB5(_1bit_registor_1_outb5),
    .OutB6(_1bit_registor_1_outb6), .OutB7(_1bit_registor_1_outb7), .OutB8(_1bit_registor_1_outb8),
    .OutB9(_1bit_registor_1_outb9), .OutB10(_1bit_registor_1_outb10), .OutB11(_1bit_registor_1_outb11),
    .OutB12(_1bit_registor_1_outb12), .OutB13(_1bit_registor_1_outb13), .OutB14(_1bit_registor_1_outb14),
    .OutB15(_1bit_registor_1_outb15), .OutB16(_1bit_registor_1_outb16));
  assign driver_1_out = decoder_1_plus ? _16bite_sumator_1_out15 : 1'bz;  // Driver driver_1
  assign driver_2_out = decoder_1_plus ? _16bite_sumator_1_out16 : 1'bz;  // Driver driver_2
  assign driver_3_out = decoder_1_plus ? _16bite_sumator_1_out13 : 1'bz;  // Driver driver_3
  assign driver_4_out = decoder_1_plus ? _16bite_sumator_1_out14 : 1'bz;  // Driver driver_4
  LED led_1 (.in(_16bite_sumator_1_out_cary));
  assign driver_5_out = decoder_1_plus ? _16bite_sumator_1_out11 : 1'bz;  // Driver driver_5
  assign driver_6_out = decoder_1_plus ? _16bite_sumator_1_out12 : 1'bz;  // Driver driver_6
  assign driver_7_out = decoder_1_plus ? _16bite_sumator_1_out9 : 1'bz;  // Driver driver_7
  assign driver_8_out = decoder_1_plus ? _16bite_sumator_1_out10 : 1'bz;  // Driver driver_8
  assign driver_9_out = decoder_1_plus ? _16bite_sumator_1_out7 : 1'bz;  // Driver driver_9
  assign driver_10_out = decoder_1_plus ? _16bite_sumator_1_out8 : 1'bz;  // Driver driver_10
  assign driver_11_out = decoder_1_plus ? _16bite_sumator_1_out5 : 1'bz;  // Driver driver_11
  assign driver_12_out = decoder_1_plus ? _16bite_sumator_1_out6 : 1'bz;  // Driver driver_12
  assign driver_13_out = decoder_1_plus ? _16bite_sumator_1_out3 : 1'bz;  // Driver driver_13
  assign driver_14_out = decoder_1_plus ? _16bite_sumator_1_out4 : 1'bz;  // Driver driver_14
  assign driver_15_out = decoder_1_plus ? _16bite_sumator_1_out1 : 1'bz;  // Driver driver_15
  assign driver_16_out = decoder_1_plus ? _16bite_sumator_1_out2 : 1'bz;  // Driver driver_16
  _16bite_sumator _16bite_sumator_1 (
    .B16(_1bit_registor_1_outb16), .B15(_1bit_registor_1_outb15), .B14(_1bit_registor_1_outb14),
    .B13(_1bit_registor_1_outb13), .B12(_1bit_registor_1_outb12), .B11(_1bit_registor_1_outb11),
    .B10(_1bit_registor_1_outb10), .B9(_1bit_registor_1_outb9), .B8(_1bit_registor_1_outb8),
    .B7(_1bit_registor_1_outb7), .B6(_1bit_registor_1_outb6), .B5(_1bit_registor_1_outb5),
    .B4(_1bit_registor_1_outb4), .B3(_1bit_registor_1_outb3), .B2(_1bit_registor_1_outb2),
    .B1(_1bit_registor_1_outb1), .A16(multiplexor_8_couta), .A15(multiplexor_7_couta),
    .A14(multiplexor_6_couta), .A13(multiplexor_5_couta), .A12(multiplexor_4_couta),
    .A11(multiplexor_3_couta), .A10(multiplexor_2_couta), .A9(multiplexor_1_couta),
    .A8(multiplexor_16_couta), .A7(multiplexor_15_couta), .A6(multiplexor_14_couta),
    .A5(multiplexor_13_couta), .A4(multiplexor_12_couta), .A3(multiplexor_11_couta),
    .A2(multiplexor_10_couta), .A1(multiplexor_9_couta), .Cary(decoder_1_plus),
    .Out_cary(_16bite_sumator_1_out_cary), .Out16(_16bite_sumator_1_out16), .Out15(_16bite_sumator_1_out15),
    .Out14(_16bite_sumator_1_out14), .Out13(_16bite_sumator_1_out13), .Out12(_16bite_sumator_1_out12),
    .Out11(_16bite_sumator_1_out11), .Out10(_16bite_sumator_1_out10), .Out9(_16bite_sumator_1_out9),
    .Out8(_16bite_sumator_1_out8), .Out7(_16bite_sumator_1_out7), .Out6(_16bite_sumator_1_out6),
    .Out5(_16bite_sumator_1_out5), .Out4(_16bite_sumator_1_out4), .Out3(_16bite_sumator_1_out3),
    .Out2(_16bite_sumator_1_out2), .Out1(_16bite_sumator_1_out1));
endmodule
